# Fritzing sketch arduino_lcd_clock (saved by Fritzing 0.9.3b)
circuit board: 8.2cm x 3.8cm
breadboards: 1

parts:
  R1 = Resistor [tolerance=±5% resistance=220 package=THT]
  Rotarry = female pin header, 5 pins [form="♀ (female)"]
  R3 = Resistor [tolerance=±5% resistance=220 package=THT]
  Poty = Rotary Potentiometer (Large) [maximum_resistance=100kΩ package=THT]
  Buzzer = Piezo Speaker
  RGB_LED = RGB LED (com. cathode, rbg) [package="5 mm [THT]"]
  RTC = ZS-042 RTC Module
  R2 = Resistor [tolerance=±5% resistance=220 package=THT]
  LCD1 = LCD screen
  Arduino_Nano = Arduino Nano (Rev3.0)

nets:
  N1: R1.Pin_0, RGB_LED.red_anode
  N2: R1.Pin_1, Arduino_Nano.A2
  GND: Rotarry.pin1, Poty.leg1, Buzzer.pin1, RGB_LED.blue_anode, RTC.GND, LCD1.VSS, LCD1.R/W, LCD1.LED-, Arduino_Nano.GND
  VCC: Rotarry.pin2, Poty.leg2, RTC.VCC, LCD1.VDD, Arduino_Nano.5V
  N3: Rotarry.pin3, Arduino_Nano.D2
  N4: Rotarry.pin4, Arduino_Nano.D8
  N5: Rotarry.pin5, Arduino_Nano.D7
  N6: R3.Pin_0, RGB_LED.green_anode
  N7: R3.Pin_1, Arduino_Nano.A0
  N8: Poty.wiper, LCD1.V0
  N9: Buzzer.pin2, Arduino_Nano.D9
  N10: RGB_LED.common_cathode, R2.Pin_0
  N11: RTC.SDA, Arduino_Nano.A4
  N12: RTC.SCL, Arduino_Nano.A5
  N13: R2.Pin_1, Arduino_Nano.A1
  N14: LCD1.RS, Arduino_Nano.D12/MISO
  N15: LCD1.E, Arduino_Nano.D11/MOSI
  N16: LCD1.DB4, Arduino_Nano.D6
  N17: LCD1.DB5, Arduino_Nano.D5
  N18: LCD1.DB6, Arduino_Nano.D4
  N19: LCD1.DB7, Arduino_Nano.D3
  N20: LCD1.LED+, Arduino_Nano.D10
